# Fritzing sketch LCD (saved by Fritzing 0.9.3b)
breadboards: 1

parts:
  Componente1 = Arduino Uno (Rev3)
  LCD1 = LCD screen
  R1 = Resistor [tolerance=±5% resistance=220 package=THT]
  R2 = Rotary Potentiometer (Small) [maximum_resistance=100kΩ package=THT]

nets:
  GND: Componente1.GND, LCD1.VSS, LCD1.R/W, R1.Pin_0, R2.leg2
  N1: Componente1.D2, LCD1.RS
  N2: Componente1.D3_PWM, LCD1.E
  N3: Componente1.D4, LCD1.DB4
  N4: Componente1.D5_PWM, LCD1.DB5
  N5: Componente1.D6_PWM, LCD1.DB6
  N6: Componente1.D7, LCD1.DB7
  5V: Componente1.5V, LCD1.VDD, LCD1.LED+, R2.leg1
  N7: LCD1.V0, R2.wiper
  N8: LCD1.LED-, R1.Pin_1
